// Logisim project marie.circ as structural Verilog: 1 circuit, main circuit main
module main (
  input  Run_Step,
  input  in_2,
  input  in_3,
  input  in_4,
  input  in_5,
  input  in_6,
  input  in_7,
  input  in_8,
  input  in_9,
  input  in_10,
  input  in_11,
  input  in_12,
  input  in_13,
  input  in_14,
  input  in_15,
  input  in_16,
  input  in_17,
  input  in_18,
  input  in_19,
  input  in_20,
  input  in_21,
  input  in_22,
  input  in_23,
  input  in_24,
  input  in_25,
  input  in_26,
  input  in_27,
  input  in_28,
  input  in_29,
  input  in_30,
  input  in_31,
  input  in_32,
  input  in_33,
  input  in_34,
  input  in_35,
  input  in_36,
  input  in_37,
  input  in_38,
  input  in_39,
  input  in_40,
  input  in_41,
  input  in_42,
  input  in_43,
  input  in_44,
  input  in_45,
  input  in_46,
  input  in_47,
  input  in_48,
  input  in_49,
  input  in_50
);

  wire ACI, ACO, ALUO, and_1_out, and_2_out, and_3_out, button_2_out, button_3_out, CE, CLK, clock_1_out, CO,
       controlled_buffer_20_out, controlled_buffer_23_out, HLT, II, INPUT, IO, JMP, MBRI, MBRO, MCR, MI,
       nor_1_out, not_1_out, not_2_out, not_3_out, not_4_out, not_5_out, OI, ONE, or_1_out, or_2_out, RI, RO,
       RST, SC, SU;
  wire [3:0] controlled_buffer_22_out, counter_1_q;
  wire [11:0] counter_2_q, multiplexer_3_out, register_2_q;
  wire [15:0] adder_1_out, BUS, controlled_inverter_1_out, multiplexer_2_out, ram_1_data, register_1_q,
       register_3_q, register_4_q;
  wire [23:0] rom_1_data;

  Button button_1 (.out(RST));
  assign HLT = in_14 ? in_16 : 1'bz;  // Controlled_Buffer controlled_buffer_1
  assign MI = in_14 ? in_17 : 1'bz;  // Controlled_Buffer controlled_buffer_2
  assign RI = in_14 ? in_18 : 1'bz;  // Controlled_Buffer controlled_buffer_3
  assign RO = in_14 ? in_19 : 1'bz;  // Controlled_Buffer controlled_buffer_4
  assign JMP = in_14 ? in_20 : 1'bz;  // Controlled_Buffer controlled_buffer_5
  assign CE = in_14 ? in_21 : 1'bz;  // Controlled_Buffer controlled_buffer_6
  assign CO = in_14 ? in_22 : 1'bz;  // Controlled_Buffer controlled_buffer_7
  assign ACI = in_14 ? in_23 : 1'bz;  // Controlled_Buffer controlled_buffer_8
  assign ACO = in_14 ? in_24 : 1'bz;  // Controlled_Buffer controlled_buffer_9
  assign SC = in_14 ? in_41 : 1'bz;  // Controlled_Buffer controlled_buffer_10
  assign SU = in_14 ? in_42 : 1'bz;  // Controlled_Buffer controlled_buffer_11
  assign MBRO = in_14 ? in_43 : 1'bz;  // Controlled_Buffer controlled_buffer_12
  assign MBRI = in_14 ? in_44 : 1'bz;  // Controlled_Buffer controlled_buffer_13
  assign OI = in_14 ? in_45 : 1'bz;  // Controlled_Buffer controlled_buffer_14
  assign ALUO = in_14 ? in_46 : 1'bz;  // Controlled_Buffer controlled_buffer_15
  assign IO = in_14 ? in_47 : 1'bz;  // Controlled_Buffer controlled_buffer_16
  assign II = in_14 ? in_48 : 1'bz;  // Controlled_Buffer controlled_buffer_17
  assign MCR = in_14 ? in_49 : 1'bz;  // Controlled_Buffer controlled_buffer_18
  assign ONE = in_14 ? in_50 : 1'bz;  // Controlled_Buffer controlled_buffer_19
  assign controlled_buffer_20_out = CLK ? MCR : 1'bz;  // Controlled_Buffer controlled_buffer_20
  Counter #(.width(4), .max('hf), .ongoal("continue")) counter_1 (
    .count(1'b1), .Q(counter_1_q), .clk(CLK), .clr(or_1_out));  // open: load, D, carry
  or or_1 (or_1_out, controlled_buffer_20_out, RST);
  DotMatrix #(.matrixcols(4), .matrixrows(1)) dotmatrix_1 (
    .col0(register_1_q[15]), .col1(register_1_q[14]), .col2(register_1_q[13]), .col3(register_1_q[12]));
  Register #(.width(16)) register_1 (.D(BUS), .en(II), .Q(register_1_q), .clk(CLK), .clr(RST));
  Clock clock_1 (.out(clock_1_out));
  Button button_2 (.out(button_2_out));
  DotMatrix #(.matrixcols(12), .matrixrows(1)) dotmatrix_2 (
    .col0(register_1_q[11]), .col1(register_1_q[10]), .col2(register_1_q[9]), .col3(register_1_q[8]),
    .col4(register_1_q[7]), .col5(register_1_q[6]), .col6(register_1_q[5]), .col7(register_1_q[4]),
    .col8(register_1_q[3]), .col9(register_1_q[2]), .col10(register_1_q[1]), .col11(register_1_q[0]));
  Multiplexer multiplexer_1 (.in0(clock_1_out), .in1(button_2_out), .out(CLK), .sel(Run_Step), .en(not_1_out));
  assign BUS = IO ? {4'b0000, register_1_q[11:0]} : 16'bz;  // Controlled_Buffer controlled_buffer_21
  not not_1 (not_1_out, HLT);
  Register #(.width(12)) register_2 (.D(BUS[11:0]), .en(MI), .Q(register_2_q), .clk(CLK), .clr(RST));
  ROM #(.dataWidth(24)) rom_1 (.addr({register_1_q[15:12], counter_1_q}), .data(rom_1_data), .sel(1'b1));
  LED #(.active("false")) led_1 (.in(in_15));
  LED led_2 (.in(in_15));
  not not_2 (not_2_out, in_15);
  Multiplexer #(.width(16)) multiplexer_2 (
    .in0(BUS),
    .in1({in_25, in_26, in_27, in_28, in_29, in_30, in_31, in_32, in_33, in_34, in_35, in_36, in_37, in_38, in_39, in_40}),
    .out(multiplexer_2_out), .sel(not_2_out), .en(1'b1));
  assign {HLT, MI, RI, RO, JMP, CE, CO, ACI, ACO, SC, SU, ALUO, MBRO, MBRI, OI, IO, II, MCR, ONE, INPUT, controlled_buffer_22_out} = not_3_out ? rom_1_data : 24'bz;  // Controlled_Buffer controlled_buffer_22
  Multiplexer #(.width(12)) multiplexer_3 (
    .in0({in_2, in_3, in_4, in_5, in_6, in_7, in_8, in_9, in_10, in_11, in_12, in_13}), .in1(register_2_q),
    .out(multiplexer_3_out), .sel(in_15), .en(1'b1));
  not not_3 (not_3_out, in_14);
  DotMatrix #(.matrixcols(16), .matrixrows(1)) dotmatrix_3 (
    .col0(BUS[15]), .col1(BUS[14]), .col2(BUS[13]), .col3(BUS[12]), .col4(BUS[11]), .col5(BUS[10]),
    .col6(BUS[9]), .col7(BUS[8]), .col8(BUS[7]), .col9(BUS[6]), .col10(BUS[5]), .col11(BUS[4]),
    .col12(BUS[3]), .col13(BUS[2]), .col14(BUS[1]), .col15(BUS[0]));
  Pull_Resistor pull_resistor_1 (.node(BUS));
  DotMatrix #(.matrixcols(12), .matrixrows(1)) dotmatrix_4 (
    .col0(multiplexer_3_out[11]), .col1(multiplexer_3_out[10]), .col2(multiplexer_3_out[9]),
    .col3(multiplexer_3_out[8]), .col4(multiplexer_3_out[7]), .col5(multiplexer_3_out[6]),
    .col6(multiplexer_3_out[5]), .col7(multiplexer_3_out[4]), .col8(multiplexer_3_out[3]),
    .col9(multiplexer_3_out[2]), .col10(multiplexer_3_out[1]), .col11(multiplexer_3_out[0]));
  assign controlled_buffer_23_out = RI ? CLK : 1'bz;  // Controlled_Buffer controlled_buffer_23
  not not_4 (not_4_out, controlled_buffer_23_out);
  Pull_Resistor pull_resistor_2 (.node(controlled_buffer_23_out));
  assign BUS = ONE ? 16'h1 : 16'bz;  // Controlled_Buffer controlled_buffer_24
  DotMatrix #(.matrixcols(16), .matrixrows(1)) dotmatrix_5 (
    .col0(ram_1_data[15]), .col1(ram_1_data[14]), .col2(ram_1_data[13]), .col3(ram_1_data[12]),
    .col4(ram_1_data[11]), .col5(ram_1_data[10]), .col6(ram_1_data[9]), .col7(ram_1_data[8]),
    .col8(ram_1_data[7]), .col9(ram_1_data[6]), .col10(ram_1_data[5]), .col11(ram_1_data[4]),
    .col12(ram_1_data[3]), .col13(ram_1_data[2]), .col14(ram_1_data[1]), .col15(ram_1_data[0]));
  RAM #(.addrWidth(12), .dataWidth(16), .bus("separate")) ram_1 (
    .addr(multiplexer_3_out), .din(multiplexer_2_out), .data(ram_1_data), .str(controlled_buffer_23_out),
    .sel(1'b1), .clk(controlled_buffer_23_out), .ld(not_4_out), .clr(1'b0));
  assign controlled_buffer_23_out = button_3_out ? 1'b1 : 1'bz;  // Controlled_Buffer controlled_buffer_25
  assign BUS = RO ? ram_1_data : 16'bz;  // Controlled_Buffer controlled_buffer_26
  Button button_3 (.out(button_3_out));
  assign controlled_inverter_1_out = SU ? ~register_3_q : 16'bz;  // Controlled_Inverter controlled_inverter_1
  not not_5 (not_5_out, SU);
  assign controlled_inverter_1_out = not_5_out ? register_3_q : 16'bz;  // Controlled_Buffer controlled_buffer_27
  assign BUS = MBRO ? register_3_q : 16'bz;  // Controlled_Buffer controlled_buffer_28
  Register #(.width(16)) register_3 (.D(BUS), .en(MBRI), .Q(register_3_q), .clk(CLK), .clr(RST));
  assign BUS = ACO ? register_4_q : 16'bz;  // Controlled_Buffer controlled_buffer_29
  Register #(.width(16)) register_4 (.D(BUS), .en(ACI), .Q(register_4_q), .clk(CLK), .clr(RST));
  Adder #(.width(16)) adder_1 (
    .a(register_4_q), .b(controlled_inverter_1_out), .out(adder_1_out), .cin(SU));  // open: cout
  Counter #(.width(12), .max('hfff), .ongoal("continue")) counter_2 (
    .load(JMP), .D(BUS[11:0]), .count(CE), .Q(counter_2_q), .clk(CLK), .clr(RST));  // open: carry
  assign BUS[11:0] = CO ? counter_2_q : 12'bz;  // Controlled_Buffer controlled_buffer_30
  DotMatrix #(.matrixcols(16), .matrixrows(1)) dotmatrix_6 (
    .col0(register_4_q[15]), .col1(register_4_q[14]), .col2(register_4_q[13]), .col3(register_4_q[12]),
    .col4(register_4_q[11]), .col5(register_4_q[10]), .col6(register_4_q[9]), .col7(register_4_q[8]),
    .col8(register_4_q[7]), .col9(register_4_q[6]), .col10(register_4_q[5]), .col11(register_4_q[4]),
    .col12(register_4_q[3]), .col13(register_4_q[2]), .col14(register_4_q[1]), .col15(register_4_q[0]));
  DotMatrix #(.matrixcols(16), .matrixrows(1)) dotmatrix_7 (
    .col0(adder_1_out[15]), .col1(adder_1_out[14]), .col2(adder_1_out[13]), .col3(adder_1_out[12]),
    .col4(adder_1_out[11]), .col5(adder_1_out[10]), .col6(adder_1_out[9]), .col7(adder_1_out[8]),
    .col8(adder_1_out[7]), .col9(adder_1_out[6]), .col10(adder_1_out[5]), .col11(adder_1_out[4]),
    .col12(adder_1_out[3]), .col13(adder_1_out[2]), .col14(adder_1_out[1]), .col15(adder_1_out[0]));
  assign BUS = ALUO ? adder_1_out : 16'bz;  // Controlled_Buffer controlled_buffer_31
  DotMatrix #(.matrixcols(16), .matrixrows(1)) dotmatrix_8 (
    .col0(register_3_q[15]), .col1(register_3_q[14]), .col2(register_3_q[13]), .col3(register_3_q[12]),
    .col4(register_3_q[11]), .col5(register_3_q[10]), .col6(register_3_q[9]), .col7(register_3_q[8]),
    .col8(register_3_q[7]), .col9(register_3_q[6]), .col10(register_3_q[5]), .col11(register_3_q[4]),
    .col12(register_3_q[3]), .col13(register_3_q[2]), .col14(register_3_q[1]), .col15(register_3_q[0]));
  DotMatrix #(.matrixcols(12), .matrixrows(1)) dotmatrix_9 (
    .col0(counter_2_q[11]), .col1(counter_2_q[10]), .col2(counter_2_q[9]), .col3(counter_2_q[8]),
    .col4(counter_2_q[7]), .col5(counter_2_q[6]), .col6(counter_2_q[5]), .col7(counter_2_q[4]),
    .col8(counter_2_q[3]), .col9(counter_2_q[2]), .col10(counter_2_q[1]), .col11(counter_2_q[0]));
  Register #(.width(16)) register_5 (.D(BUS), .en(OI), .clk(CLK), .clr(RST));  // open: Q
  nor nor_1 (nor_1_out, register_4_q[0], register_4_q[1], register_4_q[2], register_4_q[3], register_4_q[4], register_4_q[5], register_4_q[6], register_4_q[7], register_4_q[8], register_4_q[9], register_4_q[10], register_4_q[11], register_4_q[12], register_4_q[13], register_4_q[14], register_4_q[15]);
  and and_1 (and_1_out, register_4_q[15], ~BUS[11], ~BUS[10]);  // AND_Gate
  and and_2 (and_2_out, nor_1_out, ~BUS[11], BUS[10]);  // AND_Gate
  and and_3 (and_3_out, ~nor_1_out, ~register_4_q[15], BUS[11], ~BUS[10]);  // AND_Gate
  assign CE = SC ? or_2_out : 1'bz;  // Controlled_Buffer controlled_buffer_32
  or or_2 (or_2_out, and_1_out, and_2_out, and_3_out);

  // Other names for the same wires on the sheet: MANUAL = in_14; PGRM_RUN = in_15

  // Notes on the sheet:
  //   Reset
  //   Step
  //   Clock
  //   Instruction Register
  //   contents of rom_1 (hex, n*v repeats v):
  //   420000 100080 40000 20400 400100 200800 500 10020 11000 88000 6*0 420000 100080 40000 400100 100400
  //   10800 40 9*0 420000 100080 40000 400100 8400 200800 40 9*0 420000 100080 40000 400100 100400 11000
  //   40 9*0 420000 100080 40000 400100 100400 13000 40 9*0 420000 100080 40000 13*0 420000 100080 40000
  //   13*0 420000 100080 40000 800000 12*0 420000 100080 40000 4100 40 11*0 420000 100080 40000 80100 40
  //   11*0 420000 100080 40000 10000 40 11*0 420000 100080 40000 400100 100400 400800 100400 11000 40 7*0
  //   420000 100080 40000 400100 100400 80800 40 9*0 420000 100080 40000 400100 100400 400800 100400 10800
  //   8*0 420000 100080 40000 400100 100400 400800 8400 200800 8*0 420000 100080 40000
  //   Main Memory
  //   Accumulator
  //   ALU
  //   MBR
  //   Program Counter
  //   Output Register
  //   SC 000 (AC < 0)
  //   SC 800 (AC > 0)
  //   SC 400 (AC = 0)
endmodule
